# Fritzing sketch shield (saved by Fritzing 0.8.5b)
perfboards: 1

parts:
  Composants1 = Arduino Uno (Rev3)  # not connected
  LCD1 = LCD screen  # not connected
  R1 = Resistor [tolerance=±5% resistance=330 package=THT]
  R2 = Resistor [tolerance=±5% resistance=110 package=THT]
  C1 = Ceramic Capacitor [capacitance=100nF package="100 mil [THT, multilayer]"]
  S2 = Pushbutton [package=THT]
  S3 = Pushbutton [package=THT]
  C2 = Ceramic Capacitor [capacitance=100nF package="100 mil [THT, multilayer]"]
  R3 = Resistor [tolerance=±5% resistance=220 package=THT]
  S4 = Pushbutton [package=THT]
  C3 = Ceramic Capacitor [capacitance=100nF package="100 mil [THT, multilayer]"]
  R4 = Resistor [tolerance=±5% resistance=660 package=THT]
  C4 = Ceramic Capacitor [capacitance=100nF package="100 mil [THT, multilayer]"]
  S5 = Pushbutton [package=THT]
  R5 = Resistor [tolerance=±5% resistance=10k package=THT]  # not connected
  M1 = DC Motor
  Q1 = NPN-Transistor [package="TO92 [THT]"]
  VCC1 = Battery
  D1 = Rectifier Diode [part_number=1N4001 package="300 mil [THT]"]  # not connected
  C5 = Ceramic Capacitor [capacitance=100nF package="100 mil [THT, multilayer]"]

nets:
  N1: R1.Pin_1, R2.Pin_1, C1.1, S2.leg0
  N2: R2.Pin_0, S3.leg0, C2.1, R3.Pin_1
  N3: C1.0, S2.leg1, S4.leg0, C3.1
  N4: S3.leg1, C2.0, C4.1, S5.leg0
  N5: R3.Pin_0, S4.leg1, C3.0, R4.Pin_1
  N6: R4.Pin_0, S5.leg1
  N7: M1.pin_2, Q1.C, C5.1
  N8: Q1.E, Q1.B, VCC1.-
